# Fritzing sketch arms_shadowDetect (saved by Fritzing 0.9.3b)
breadboards: 1

parts:
  Part1 = Arduino Uno (Rev3)
  R1 = Photocell (LDR) [package=THT]
  R2 = Resistor [tolerance=±5% resistance=220 package=THT]
  LED1 = LED - 5mm [color="Red (633nm)" package="5 mm [THT]"]

nets:
  N1: Part1.A1, R1.pin_1, R2.Pin_0
  N2: Part1.D8, LED1.anode
  N3: Part1.GND, R2.Pin_1, LED1.cathode
  N4: Part1.5V, R1.pin_0
